# Fritzing sketch wiring diagram (saved by Fritzing 0.9.9b)

parts:
  Ac_Power = Power plug
  HLK-PM1 = HLK-PM01
  Part1 = IFR520 MOS module [package=THT]
  Part2 = IFR520 MOS module [package=THT]
  Part3 = IFR520 MOS module [package=THT]
  Part4 = IFR520 MOS module [package=THT]
  Mod1 = Raspberry Pi Pico
  M1 = RioRand LM2596
  HLK-PM3 = HLK-PM12 [part_number=HLK-PM12]
  Part5 = IFR520 MOS module [package=THT]
  Part6 = IFR520 MOS module [package=THT]
  Part7 = IFR520 MOS module [package=THT]
  Part8 = IFR520 MOS module [package=THT]
  Part9 = IFR520 MOS module [package=THT]
  Part10 = IFR520 MOS module [package=THT]
  Part11 = IFR520 MOS module [package=THT]
  Part12 = IFR520 MOS module [package=THT]
  Part13 = IFR520 MOS module [package=THT]  # not connected
  Part14 = IFR520 MOS module [package=THT]  # not connected
  Part15 = IFR520 MOS module [package=THT]  # not connected
  Part16 = IFR520 MOS module [package=THT]  # not connected

nets:
  N1: Ac_Power.GND, HLK-PM1.AC#1, HLK-PM3.AC_2
  N2: Ac_Power.VCC, HLK-PM1.AC#0, HLK-PM3.AC_1
  N3: Part1.SIG, Mod1.pin_1
  VCC: Part1.VCC, Part2.VCC, Part3.VCC, Part4.VCC, Mod1.pin_36, Part5.VCC, Part6.VCC, Part7.VCC, Part8.VCC, Part9.VCC, Part10.VCC, Part11.VCC, Part12.VCC
  GND: Part1.GND, Part2.GND, Part3.GND, Part4.GND, Mod1.pin_3, Mod1.pin_8, Mod1.pin_13, Part6.SIG, Part9.GND, Part10.GND, Part11.GND, Part12.GND
  N4: Part1.V+, M1.Pin_3
  N5: Part1.V-, M1.Pin_4
  N6: Part2.SIG, Mod1.pin_2
  N7: Part3.SIG, Mod1.pin_4
  N8: Part4.SIG, Mod1.pin_5
  N9: Mod1.pin_6, Part8.SIG
  N10: Mod1.pin_7, Part7.SIG
  GND_2: Mod1.pin_9, Part5.GND, Part6.GND, Part7.GND, Part8.GND
  N11: Mod1.pin_10, Part5.SIG
  N12: Mod1.pin_11, Part12.SIG
  N13: Mod1.pin_12, Part11.SIG
  N14: Mod1.pin_14, Part10.SIG
  N15: Mod1.pin_15, Part9.SIG
  N16: M1.Pin_1, HLK-PM3.+Vo
  N17: M1.Pin_2, HLK-PM3.-Vo

notes:
  Ac Power
  OUTPUT : 24VDC

custom parts:
  Raspberry Pi Pico: Raspberry Pi Pico. Based around the RP2040 microcontroller the Pico is a low cost microcontroller device bringing Raspberry Pi quality, cost, and easy of use to the microcontroller space. Jan 2021, Split part in to two versions: tht (this one) and SMD. This one will drill holes for a .1 in header in pcb to allow plugging in the module as well as providing pads to solder the module to the top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
